# Fritzing sketch Esquema de conexiones (saved by Fritzing 0.9.3b)
breadboards: 2

parts:
  Raspberry_Pi1 = Raspberry Pi B+
  Pololu_A1 = Pololu A4988 [package=SO16]
  M1 = Stepper Motor - Bipolar
  LED1 = RGB LED (com. cathode, rbg) [package="5 mm [THT]"]
  R1 = Resistor [tolerance=±5% resistance=220 package="0805 [SMD]"]
  R4 = Resistor [tolerance=±5% resistance=220 package="0805 [SMD]"]
  R5 = Resistor [tolerance=±5% resistance=220 package="0805 [SMD]"]
  Componente1 = LCD1602-I2C
  C1 = Capacitor Polarized [package=panasonic_c]
  J3 = Power Jack [package=power_jack_smd]
  J4 = Basic Servo
  R7 = Resistor [tolerance=±5% resistance=220 package="0805 [SMD]"]
  LED3 = smd LED [color="Red (633nm)" package="0805 [SMD]"]
  S1 = Pushbutton [package="[SMD]"]
  S2 = Pushbutton [package="[SMD]"]
  CAMERA1 = TTL Serial JPEG Camera  # not connected

nets (from the breadboard view):
  N1: Raspberry_Pi1.GPIO2, Componente1.SDA
  N2: Raspberry_Pi1.GPIO3, Componente1.SCL
  N3: Raspberry_Pi1.GPIO17, Pololu_A1.DIR
  N4: Raspberry_Pi1.GPIO27, Pololu_A1.STEP
  N5: Raspberry_Pi1.GPIO5, Pololu_A1.MS1
  N6: Raspberry_Pi1.GPIO6, Pololu_A1.MS2
  N7: Raspberry_Pi1.GPIO13, Pololu_A1.MS3
  N8: Raspberry_Pi1.GPIO19, S2.Pin_1, S2.Pin_2
  N9: Raspberry_Pi1.GPIO26, S1.Pin_1, S1.Pin_2
  N10: Raspberry_Pi1.GPIO21, R1.Pin_1
  N11: Raspberry_Pi1.GPIO20, R4.Pin_1
  N12: Raspberry_Pi1.GPIO16, R5.Pin_1
  GND: Raspberry_Pi1.GND, Pololu_A1.GND#8, LED1.common_cathode, Componente1.GND, J4.gnd, LED3.anode, S1.Pin_3, S1.Pin_4, S2.Pin_3, S2.Pin_4
  N13: Raspberry_Pi1.GPIO12, R7.Pin_1
  N14: Raspberry_Pi1.GPIO14, J4.pulse
  VCC: Raspberry_Pi1.5V, Pololu_A1.VDD, Componente1.VCC, J4.vcc
  N15: Pololu_A1.RESET, Pololu_A1.SLEEP
  N16: Pololu_A1.1B, M1.D
  N17: Pololu_A1.1A, M1.C
  N18: Pololu_A1.2A, M1.B
  N19: Pololu_A1.2B, M1.A
  N20: Pololu_A1.GND#14, C1.-, J3.GND
  N21: Pololu_A1.VMOT, C1.+, J3.PWR
  N22: LED1.red_anode, R5.Pin_0
  N23: LED1.blue_anode, R4.Pin_0
  N24: LED1.green_anode, R1.Pin_0
  N25: R7.Pin_0, LED3.cathode

custom parts:
  LCD1602-I2C: A standard character display, usually with 2x16 characters. Comes in many colors with LCM1602 IIC attached.
  TTL Serial JPEG Camera: TTL Serial JPEG Camera with NTSC Out
